# Fritzing sketch 7 segments fritzing file (saved by Fritzing 0.9.3b)
breadboards: 1

parts:
  Part1 = Arduino Nano (Rev3.0)
  DI1 = 7-Segment LED Display [package=THT]
  DI2 = 7-Segment LED Display [package=THT]

nets:
  N1: Part1.D1/TX, DI1.cathodeA, DI2.cathodeG
  N2: Part1.D0/RX, DI2.commAnode#7
  N3: Part1.D2, DI1.cathodeB
  N4: Part1.D3, DI1.commAnode#2, DI2.cathodeF
  N5: Part1.D4, DI1.cathodeD, DI2.cathodeD
  N6: Part1.D5, DI1.cathodeC, DI2.commAnode#2
  N7: Part1.D6, DI1.cathodeE, DI2.cathodeE, DI2.cathodeDP
  N8: Part1.D8, DI1.cathodeF
  N9: Part1.D9, DI1.cathodeG, DI2.cathodeB
