# Fritzing sketch dobbelsteen fritz (saved by Fritzing 0.9.3b)
breadboards: 1

parts:
  Part1 = Arduino Nano (Rev3.0)
  R1 = Resistor [tolerance=±5% resistance=220 package="1206 [SMD]"]
  R2 = Resistor [tolerance=±5% resistance=220 package="1206 [SMD]"]
  R3 = Resistor [tolerance=±5% resistance=220 package="1206 [SMD]"]
  LED1 = smd LED [color="Orange (620nm)" package="1206 [SMD]"]
  LED2 = smd LED [color="Red (660nm)" package="1206 [SMD]"]
  LED3 = smd LED [color="Infrared (940nm)" package="1206 [SMD]"]
  LED4 = smd LED [color="Red (660nm)" package="1206 [SMD]"]
  LED5 = smd LED [color="Orange (620nm)" package="1206 [SMD]"]
  LED6 = smd LED [color="Infrared (940nm)" package="1206 [SMD]"]
  LED7 = smd LED [color="Red (660nm)" package="1206 [SMD]"]
  LED8 = smd LED [color="Orange (620nm)" package="1206 [SMD]"]
  LED9 = smd LED [color="Infrared (940nm)" package="1206 [SMD]"]
  S1 = Round Pushbutton

nets:
  N1: Part1.D2, S1.leg0
  N2: Part1.D8, LED7.cathode, LED8.cathode, LED9.cathode
  N3: Part1.D9, LED1.cathode, LED2.cathode, LED3.cathode
  N4: Part1.D10, LED4.cathode, LED5.cathode, LED6.cathode
  N5: Part1.A2, R2.Pin_1
  N6: Part1.A1, R1.Pin_1
  N7: Part1.A0, R3.Pin_1
  N8: Part1.3V3, S1.leg1
  N9: R1.Pin_0, LED7.anode
  N10: R2.Pin_0, LED8.anode
  N11: R3.Pin_0, LED9.anode
