# Fritzing sketch fritzing file (saved by Fritzing 0.9.3b)
breadboards: 1

parts:
  Part1 = Arduino Nano (Rev3.0) (ICSP)
  U1 = POT [package=alps_pot]
  C1 = Capacitor Polarized [package=cpol-radial-100uf-25v]
  J1 = Piezo Speaker

nets:
  N1: Part1.GND, U1.A, C1.-
  N2: Part1.D2, J1.pin2
  N3: Part1.5V, U1.E
  N4: Part1.A5, U1.S
  N5: C1.+, J1.pin1
