# Fritzing sketch fritzing (saved by Fritzing 0.9.3b)
breadboards: 1

parts:
  Part1 = Arduino Nano (Rev3.0)
  LED1 = RGB LED - (4 legs) [package="5 mm [THT]"]
  R1 = Resistor [tolerance=±5% resistance=220 package="0603 [SMD]"]

nets:
  N1: Part1.GND, R1.Pin_1
  N2: Part1.D9, LED1.red_cathode
  N3: Part1.D10, LED1.common_anode
  N4: Part1.D11/MOSI, LED1.blue_cathode
  N5: LED1.green_cathode, R1.Pin_0
