# Fritzing sketch fritzing (saved by Fritzing 0.9.3b)
breadboards: 1

parts:
  Part1 = Arduino Nano (Rev3.0)
  R1 = Resistor [tolerance=±5% resistance=220 package="0603 [SMD]"]
  LCD1 = LCD screen

nets:
  GND: Part1.GND, R1.Pin_0, LCD1.VSS, LCD1.R/W
  N1: Part1.D8, LCD1.DB4
  N2: Part1.D9, LCD1.DB5
  N3: Part1.D10, LCD1.DB6
  N4: Part1.D11/MOSI, LCD1.DB7
  N5: Part1.D12/MISO, LCD1.E
  5V: Part1.5V, LCD1.VDD
  N6: Part1.D13/SCK, LCD1.RS
  N7: R1.Pin_1, LCD1.V0
