# Fritzing sketch fritzing (saved by Fritzing 0.9.3b)
breadboards: 1

parts:
  LCD1 = LCD screen
  Part1 = Arduino Nano (Rev3.0) (ICSP)
  J1 = Piezo Speaker
  C1 = Capacitor Polarized [package=cpol-radial-10uf-25v]
  R1 = Resistor [tolerance=±5% resistance=220 package=THT]
  Part2 = Adafruit Thermocouple Amplifier MAX31855 [part_number="Adafruit #269"]
  R2 = Temperature Sensor (Thermistor) [thermistor_type=NTC package=THT]  # not connected

nets:
  GND: LCD1.VSS, LCD1.R/W, Part1.GND, C1.-, R1.Pin_0, Part2.GND
  VDD: LCD1.VDD, Part1.5V, Part2.VIN
  N1: LCD1.V0, R1.Pin_1
  N2: LCD1.RS, Part1.D13/SCK
  N3: LCD1.E, Part1.D12/MISO
  N4: LCD1.DB4, Part1.D8
  N5: LCD1.DB5, Part1.D9
  N6: LCD1.DB6, Part1.D10
  N7: LCD1.DB7, Part1.D11/MOSI
  N8: Part1.D3, J1.pin2
  N9: Part1.D5, Part2.DO
  N10: Part1.D6, Part2.CS
  N11: Part1.D7, Part2.CLK
  N12: J1.pin1, C1.+

custom parts:
  Adafruit Thermocouple Amplifier MAX31855: Thermocouples are very sensitive, requiring a good amplifier with a cold-compensation reference. The MAX31855K does everything for you, and can be easily interfaced with any microcontroller, even one without an analog input. This breakout board has the chip itself, a 3.3V regulator with 10uF bypass capacitors and level shifting circuitry, all assembled and tested. Comes with a 2 pin terminal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
